# Fritzing sketch Step-1 - Sensors - Circuit Design (saved by Fritzing 0.9.3b)
breadboards: 1

parts:
  hc-sr1 = hc-sr04
  Part1 = Arduino Uno (Rev3)
  R8 = Resistor [tolerance=±5% resistance=220 package=THT]
  LED1 = LED - 5mm [color="Blue (430nm)" package="5 mm [THT]"]
  R10 = Photocell (LDR) [package=THT]
  R11 = Resistor [tolerance=±5% resistance=10k package=THT]
  DHT1 = DHT11 Humitidy and Temperature Sensor
  LED2 = LED - 5mm [color="Red (635nm)" package="5 mm [THT]"]
  R12 = Resistor [tolerance=±5% resistance=220 package=THT]
  LED3 = LED - 5mm [color="Green (555nm)" package="5 mm [THT]"]
  R13 = Resistor [tolerance=±5% resistance=220 package=THT]

nets:
  VCC: hc-sr1.VCC, Part1.5V, R10.pin_0, DHT1.VDD
  N1: hc-sr1.Trig, Part1.D8
  N2: hc-sr1.Echo, Part1.D9_PWM
  GND: hc-sr1.GND, Part1.GND, R8.Pin_0, R11.Pin_1, DHT1.GND, R12.Pin_0, R13.Pin_0
  N3: Part1.A0, R10.pin_1, R11.Pin_0
  N4: Part1.D2, DHT1.DATA
  N5: Part1.D3_PWM, LED2.cathode
  N6: Part1.D4, LED3.cathode
  N7: Part1.D5_PWM, LED1.cathode
  N8: R8.Pin_1, LED1.anode
  N9: LED2.anode, R12.Pin_1
  N10: LED3.anode, R13.Pin_1

notes:
  Ultrasonic Sensor
  LDR Sensor
  HTTP
  Error
  Event
  DHT11 Sensor

custom parts:
  DHT11 Humitidy and Temperature Sensor: DHT11 Humidity and Temperature Sensor
